// Logisim project Project3Given.circ as structural Verilog: 9 circuits, main circuit CPU15
module main (
  input  EnableBreakpoint,
  input  [14:0] Breakpoint
);

  wire and_2_out, and_3_out, chipset_1_irq, CLK, clock_1_out, cpu15_1_c, cpu15_1_e, cpu15_1_i, cpu15_1_n,
       cpu15_1_o, cpu15_1_z, KBCLR, KBIRQ, KBRD, MEMCS, nand_1_out, RE, TTYCLR, TTYWE, WE;
  wire [6:0] KBDATA, TTYDATA;
  wire [7:0] cpu15_1_srf;
  wire [14:0] ADDR, chipset_1_ivect, chipset_1_led0, chipset_1_led1, chipset_1_led2, chipset_1_led3,
       chipset_1_led4, chipset_1_led5, chipset_1_led6, chipset_1_led7, chipset_1_led8, chipset_1_led9,
       chipset_1_leda, chipset_1_ledb, chipset_1_ledc, chipset_1_ledd, chipset_1_lede, cpu15_1_ib,
       cpu15_1_pc, cpu15_1_r0, cpu15_1_r1, cpu15_1_r2, cpu15_1_r3, cpu15_1_r4, cpu15_1_r5, cpu15_1_r6,
       cpu15_1_r7, cpu15_1_srp, DATA, xnor_1_out;

  Clock clock_1 (.out(clock_1_out));
  nand nand_1 (nand_1_out, EnableBreakpoint, xnor_1_out[0], xnor_1_out[1], xnor_1_out[2], xnor_1_out[3], xnor_1_out[4], xnor_1_out[5], xnor_1_out[6], xnor_1_out[7], xnor_1_out[8], xnor_1_out[9], xnor_1_out[10], xnor_1_out[11], xnor_1_out[12], xnor_1_out[13], xnor_1_out[14], 1'b1);
  and and_1 (CLK, clock_1_out, nand_1_out);
  assign xnor_1_out = ~(Breakpoint ^ cpu15_1_pc);  // XNOR_Gate xnor_1, 15 bits wide
  LED I (.in(cpu15_1_i));
  LED Z (.in(cpu15_1_z));
  LED N (.in(cpu15_1_n));
  LED O (.in(cpu15_1_o));
  LED C (.in(cpu15_1_c));
  LED E (.in(cpu15_1_e));
  and and_2 (and_2_out, WE, MEMCS);
  and and_3 (and_3_out, MEMCS, RE);
  RAM #(.addrWidth(15), .asyncread("true"), .dataWidth(15), .databus("bidir")) ram_1 (
    .addr(ADDR), .we(and_2_out), .oe(and_3_out), .clk(CLK), .data(DATA));
  // Probe on cpu15_1_pc
  // Probe on cpu15_1_ib
  // Probe on cpu15_1_srp
  // Probe on cpu15_1_srf
  // Probe on cpu15_1_r0
  // Probe on cpu15_1_r1
  // Probe on cpu15_1_r2
  // Probe on cpu15_1_r3
  // Probe on cpu15_1_r4
  // Probe on cpu15_1_r5
  // Probe on cpu15_1_r6
  // Probe on cpu15_1_r7
  CPU15 cpu15_1 (
    .I(cpu15_1_i), .Z(cpu15_1_z), .N(cpu15_1_n), .O(cpu15_1_o), .C(cpu15_1_c), .E(cpu15_1_e),
    .PC(cpu15_1_pc), .IB(cpu15_1_ib), .SRP(cpu15_1_srp), .SRF(cpu15_1_srf), .R0(cpu15_1_r0), .R1(cpu15_1_r1),
    .R2(cpu15_1_r2), .R3(cpu15_1_r3), .R4(cpu15_1_r4), .R5(cpu15_1_r5), .R6(cpu15_1_r6), .R7(cpu15_1_r7),
    .CLK(CLK), .IRQ(chipset_1_irq), .RE(RE), .WE(WE), .ADDR(ADDR), .DATAIN(DATA), .DATAOUT(DATA));
  // Probe on ADDR
  // Probe on DATA
  // Probe on chipset_1_ivect
  // Probe on TTYDATA
  CHIPSET chipset_1 (
    .RE(RE), .WE(WE), .ADDR(ADDR), .CPUDATAIN(DATA), .CPUDATAOUT(DATA), .IRQ(chipset_1_irq),
    .IVECT(chipset_1_ivect), .CLK(CLK), .MEMCS(MEMCS), .TTYWR(TTYWE), .TTYCLR(TTYCLR), .TTYDATA(TTYDATA),
    .KBRD(KBRD), .KBCLR(KBCLR), .KBIRQ(KBIRQ), .KBDATA(KBDATA), .LED0(chipset_1_led0), .LED1(chipset_1_led1),
    .LED2(chipset_1_led2), .LED3(chipset_1_led3), .LED4(chipset_1_led4), .LED5(chipset_1_led5),
    .LED6(chipset_1_led6), .LED7(chipset_1_led7), .LED8(chipset_1_led8), .LED9(chipset_1_led9),
    .LEDA(chipset_1_leda), .LEDB(chipset_1_ledb), .LEDC(chipset_1_ledc), .LEDD(chipset_1_ledd),
    .LEDE(chipset_1_lede));
  TTY tty_1 (.data(TTYDATA), .clk(CLK), .we(TTYWE), .clr(TTYCLR));
  Keyboard keyboard_1 (.clk(CLK), .re(KBRD), .clr(KBCLR), .avail(KBIRQ), .data(KBDATA));
  DotMatrix #(.matrixcols(15), .matrixrows(15)) dotmatrix_1 (
    .col0(chipset_1_led0), .col1(chipset_1_led1), .col2(chipset_1_led2), .col3(chipset_1_led3),
    .col4(chipset_1_led4), .col5(chipset_1_led5), .col6(chipset_1_led6), .col7(chipset_1_led7),
    .col8(chipset_1_led8), .col9(chipset_1_led9), .col10(chipset_1_leda), .col11(chipset_1_ledb),
    .col12(chipset_1_ledc), .col13(chipset_1_ledd), .col14(chipset_1_lede));
endmodule

// CPU
module CPU15 (
  input  [14:0] DATAIN,
  input  CLK,
  input  IRQ,
  output [14:0] PC,
  output [14:0] IB,
  output [14:0] SRP,
  output [7:0] SRF,
  output [14:0] R0,
  output [14:0] R1,
  output [14:0] R2,
  output [14:0] R3,
  output [14:0] R4,
  output [14:0] R5,
  output [14:0] R6,
  output [14:0] R7,
  output RE,
  output WE,
  output I,
  output Z,
  output [14:0] ADDR,
  output N,
  output O,
  output C,
  output E,
  output [14:0] DATAOUT
);


  // Other names for the same wires on the sheet: DATA[14:0] = DATAIN
endmodule

module CHIPSET (
  input  RE,
  input  WE,
  input  [14:0] ADDR,
  input  [14:0] CPUDATAIN,
  input  KBIRQ,
  input  [6:0] KBDATA,
  input  CLK,
  output MEMCS,
  output TTYWR,
  output [14:0] IVECT,
  output TTYCLR,
  output [6:0] TTYDATA,
  output KBRD,
  output KBCLR,
  output [14:0] CPUDATAOUT,
  output IRQ,
  output [14:0] LED0,
  output [14:0] LED1,
  output [14:0] LED2,
  output [14:0] LED3,
  output [14:0] LED4,
  output [14:0] LED5,
  output [14:0] LED6,
  output [14:0] LED7,
  output [14:0] LED8,
  output [14:0] LED9,
  output [14:0] LEDA,
  output [14:0] LEDB,
  output [14:0] LEDC,
  output [14:0] LEDD,
  output [14:0] LEDE
);

  wire and_1_out, and_8_out, and_10_out, DATA7, IOCS, IVECTADDR, IVECTEN, IVECTRE, KBCS, LED0EN, LED0END,
       LED1EN, LED1END, LED2EN, LED2END, LED3EN, LED3END, LED4EN, LED4END, LED5EN, LED5END, LED6EN, LED6END,
       LED7EN, LED7END, LED8EN, LED8END, LED9EN, LED9END, LEDAEN, LEDAEND, LEDBEN, LEDBEND, LEDCEN, LEDCEND,
       LEDCS, LEDDEN, LEDDEND, LEDEEN, LEDEEND, LEDFEND, LEDRE, multiplexer_17_out, multiplexer_18_out, RWE,
       TTYCS;
  wire [14:0] DATAL0, DATAL1, DATAL2, DATAL3, DATAL4, DATAL5, DATAL6, DATAL7, DATAL8, DATAL9, DATALA, DATALB,
       DATALC, DATALD, DATALE, LEDDATA;
  wire [14:8] KBDATA15;

  assign CPUDATAOUT = KBRD ? {KBDATA15, DATA7, KBDATA} : 15'bz;  // Controlled_Buffer controlled_buffer_1
  assign CPUDATAOUT = LEDRE ? LEDDATA : 15'bz;  // Controlled_Buffer controlled_buffer_2
  assign CPUDATAOUT = IVECTRE ? IVECT : 15'bz;  // Controlled_Buffer controlled_buffer_3
  Register #(.width(15)) register_1 (.D(DATAL0), .en(LED0EN), .Q(LED0), .clk(CLK));  // open: clr
  Register #(.width(15)) register_2 (.D(DATAL1), .en(LED1EN), .Q(LED1), .clk(CLK));  // open: clr
  Register #(.width(15)) register_3 (.D(DATAL2), .en(LED2EN), .Q(LED2), .clk(CLK));  // open: clr
  Register #(.width(15)) register_4 (.D(DATAL3), .en(LED3EN), .Q(LED3), .clk(CLK));  // open: clr
  Register #(.width(15)) register_5 (.D(DATAL4), .en(LED4EN), .Q(LED4), .clk(CLK));  // open: clr
  and and_1 (and_1_out, WE, LEDCS);
  Decoder #(.select(4)) decoder_1 (
    .out0(LED0END), .out1(LED1END), .out2(LED2END), .out3(LED3END), .out4(LED4END), .out5(LED5END),
    .out6(LED6END), .out7(LED7END), .out8(LED8END), .out9(LED9END), .out10(LEDAEND), .out11(LEDBEND),
    .out12(LEDCEND), .out13(LEDDEND), .out14(LEDEEND), .out15(LEDFEND), .sel(ADDR[3:0]), .en(and_1_out));
  Register #(.width(15)) register_6 (.D(DATAL5), .en(LED5EN), .Q(LED5), .clk(CLK));  // open: clr
  Register #(.width(15)) register_7 (.D(DATAL6), .en(LED6EN), .Q(LED6), .clk(CLK));  // open: clr
  Register #(.width(15)) register_8 (.D(DATAL7), .en(LED7EN), .Q(LED7), .clk(CLK));  // open: clr
  Register #(.width(15)) register_9 (.D(DATAL8), .en(LED8EN), .Q(LED8), .clk(CLK));  // open: clr
  Register #(.width(15)) register_10 (.D(DATAL9), .en(LED9EN), .Q(LED9), .clk(CLK));  // open: clr
  or or_1 (LED0EN, LED0END, LEDFEND);
  or or_2 (LED1EN, LED1END, LEDFEND);
  or or_3 (LED2EN, LED2END, LEDFEND);
  or or_4 (LED3EN, LED3END, LEDFEND);
  or or_5 (LED4EN, LED4END, LEDFEND);
  or or_6 (LED5EN, LED5END, LEDFEND);
  or or_7 (LED6EN, LED6END, LEDFEND);
  or or_8 (LED7EN, LED7END, LEDFEND);
  or or_9 (LED8EN, LED8END, LEDFEND);
  or or_10 (LED9EN, LED9END, LEDFEND);
  or or_11 (LEDAEN, LEDAEND, LEDFEND);
  or or_12 (LEDBEN, LEDBEND, LEDFEND);
  or or_13 (LEDCEN, LEDCEND, LEDFEND);
  or or_14 (LEDDEN, LEDDEND, LEDFEND);
  or or_15 (LEDEEN, LEDEEND, LEDFEND);
  Pull_Resistor pull_resistor_1 (.node(KBDATA15[14]));
  Pull_Resistor pull_resistor_2 (.node(KBDATA15[13]));
  Pull_Resistor pull_resistor_3 (.node(KBDATA15[12]));
  Pull_Resistor pull_resistor_4 (.node(KBDATA15[11]));
  Pull_Resistor pull_resistor_5 (.node(KBDATA15[10]));
  Pull_Resistor pull_resistor_6 (.node(KBDATA15[9]));
  Pull_Resistor pull_resistor_7 (.node(KBDATA15[8]));
  Pull_Resistor pull_resistor_8 (.node(DATA7));
  Register #(.width(15)) register_11 (.D(DATALA), .en(LEDAEN), .Q(LEDA), .clk(CLK));  // open: clr
  Register #(.width(15)) register_12 (.D(DATALB), .en(LEDBEN), .Q(LEDB), .clk(CLK));  // open: clr
  Register #(.width(15)) register_13 (.D(DATALC), .en(LEDCEN), .Q(LEDC), .clk(CLK));  // open: clr
  Register #(.width(15)) register_14 (.D(DATALD), .en(LEDDEN), .Q(LEDD), .clk(CLK));  // open: clr
  Register #(.width(15)) register_15 (.D(DATALE), .en(LEDEEN), .Q(LEDE), .clk(CLK));  // open: clr
  Multiplexer #(.width(15)) multiplexer_1 (.in0(CPUDATAIN), .in1(LED1), .out(DATAL0), .sel(LEDFEND));
  Multiplexer #(.width(15)) multiplexer_2 (.in0(CPUDATAIN), .in1(LED2), .out(DATAL1), .sel(LEDFEND));
  Multiplexer #(.width(15)) multiplexer_3 (.in0(CPUDATAIN), .in1(LED3), .out(DATAL2), .sel(LEDFEND));
  Multiplexer #(.width(15)) multiplexer_4 (.in0(CPUDATAIN), .in1(LED4), .out(DATAL3), .sel(LEDFEND));
  Multiplexer #(.width(15)) multiplexer_5 (.in0(CPUDATAIN), .in1(LED5), .out(DATAL4), .sel(LEDFEND));
  Multiplexer #(.select(4), .width(15)) multiplexer_6 (
    .in0(LED0), .in1(LED1), .in2(LED2), .in3(LED3), .in4(LED4), .in5(LED5), .in6(LED6), .in7(LED7),
    .in8(LED8), .in9(LED9), .in10(LEDA), .in11(LEDB), .in12(LEDC), .in13(LEDD), .in14(LEDE),
    .in15({15{1'b0}}), .out(LEDDATA), .sel(ADDR[3:0]));
  Multiplexer #(.width(15)) multiplexer_7 (.in0(CPUDATAIN), .in1(LED6), .out(DATAL5), .sel(LEDFEND));
  Multiplexer #(.width(15)) multiplexer_8 (.in0(CPUDATAIN), .in1(LED7), .out(DATAL6), .sel(LEDFEND));
  Multiplexer #(.width(15)) multiplexer_9 (.in0(CPUDATAIN), .in1(LED8), .out(DATAL7), .sel(LEDFEND));
  Multiplexer #(.width(15)) multiplexer_10 (.in0(CPUDATAIN), .in1(LED9), .out(DATAL8), .sel(LEDFEND));
  Multiplexer #(.width(15)) multiplexer_11 (.in0(CPUDATAIN), .in1(LEDA), .out(DATAL9), .sel(LEDFEND));
  and and_2 (LEDRE, RE, LEDCS);
  Multiplexer #(.width(15)) multiplexer_12 (.in0(CPUDATAIN), .in1(LEDB), .out(DATALA), .sel(LEDFEND));
  Multiplexer #(.width(15)) multiplexer_13 (.in0(CPUDATAIN), .in1(LEDC), .out(DATALB), .sel(LEDFEND));
  Multiplexer #(.width(15)) multiplexer_14 (.in0(CPUDATAIN), .in1(LEDD), .out(DATALC), .sel(LEDFEND));
  Multiplexer #(.width(15)) multiplexer_15 (.in0(CPUDATAIN), .in1(LEDE), .out(DATALD), .sel(LEDFEND));
  Multiplexer #(.width(15)) multiplexer_16 (.in0(CPUDATAIN), .in1(CPUDATAIN), .out(DATALE), .sel(LEDFEND));
  and and_3 (IOCS, ADDR[5], ADDR[6], ADDR[7], ADDR[8], ADDR[9], ADDR[10], ADDR[11], ADDR[12], ADDR[13], ADDR[14], 1'b1);
  and and_4 (TTYCS, IOCS, ADDR[0], ~ADDR[1], ~ADDR[2], ~ADDR[3], ADDR[4]);  // AND_Gate
  and and_5 (KBCS, IOCS, ~ADDR[0], ~ADDR[1], ~ADDR[2], ~ADDR[3], ADDR[4]);  // AND_Gate
  and and_6 (IVECTADDR, ADDR[0], ADDR[1], ADDR[2], ADDR[3], ADDR[4], ADDR[5], ADDR[6], ADDR[7], ADDR[8], ADDR[9], ADDR[10], ADDR[11], ADDR[12], ADDR[13], ADDR[14]);
  and and_7 (TTYWR, TTYCS, WE);
  and and_8 (and_8_out, TTYWR, DATA7);
  and and_9 (KBRD, KBCS, RE);
  and and_10 (and_10_out, KBCS, WE);
  Multiplexer multiplexer_17 (.in0(and_10_out), .in1(1'b0), .out(multiplexer_17_out), .sel(KBCLR));
  and and_11 (LEDCS, IOCS, ~ADDR[4], RWE);  // AND_Gate
  and and_12 (IVECTEN, IVECTADDR, WE);
  and and_13 (IVECTRE, IVECTADDR, RE);
  or or_16 (RWE, RE, WE);
  and and_14 (MEMCS, ~IOCS, RWE);  // AND_Gate
  Multiplexer multiplexer_18 (.in0(and_8_out), .in1(1'b0), .out(multiplexer_18_out), .sel(TTYCLR));
  D_Flip_Flop d_ff_1 (.clk(CLK), .D(multiplexer_17_out), .Q(KBCLR));  // open: Qn, preset, reset
  Register #(.width(15)) register_16 (.D(CPUDATAIN), .en(IVECTEN), .Q(IVECT), .clk(CLK));  // open: clr
  D_Flip_Flop d_ff_2 (.clk(CLK), .D(multiplexer_18_out), .Q(TTYCLR));  // open: Qn, preset, reset

  assign IRQ = KBIRQ;
  assign TTYDATA = CPUDATAIN[6:0];

  // Other names for the same wires on the sheet: DATA[14:0] = CPUDATAIN; KBDATA15[7:0] = {DATA7, KBDATA}
endmodule

module ADDER15 (
  input  [14:0] A,
  input  [14:0] B,
  input  CIN,
  output COUT,
  output [14:0] S
);
endmodule

module REGS15 (
  input  [14:0] D,
  input  W,
  input  [2:0] SelD,
  input  CLK,
  input  [2:0] SelA,
  input  [2:0] SelB,
  output [14:0] R0,
  output [14:0] R1,
  output [14:0] R2,
  output [14:0] R3,
  output [14:0] R4,
  output [14:0] R5,
  output [14:0] R6,
  output [14:0] R7,
  output [14:0] A,
  output [14:0] B
);

  wire W_1, W_2, W_3, W_4, W_5, W_6, W_7;

  Register #(.width(15)) register_1 (.D({15{1'b0}}), .clk(CLK), .Q(R0));  // open: en, clr
  Decoder #(.select(3)) decoder_1 (
    .out1(W_1), .out2(W_2), .out3(W_3), .out4(W_4), .out5(W_5), .out6(W_6), .out7(W_7), .sel(SelD), .en(W));  // open: out0
  Multiplexer #(.select(3), .width(15)) multiplexer_1 (
    .in0(R0), .in1(R1), .in2(R2), .in3(R3), .in4(R4), .in5(R5), .in6(R6), .in7(R7), .out(A), .sel(SelA));
  Register #(.width(15)) register_2 (.D(D), .en(W_1), .clk(CLK), .Q(R1));  // open: clr
  Register #(.width(15)) register_3 (.D(D), .en(W_2), .clk(CLK), .Q(R2));  // open: clr
  Register #(.width(15)) register_4 (.D(D), .en(W_3), .clk(CLK), .Q(R3));  // open: clr
  Multiplexer #(.select(3), .width(15)) multiplexer_2 (
    .in0(R0), .in1(R1), .in2(R2), .in3(R3), .in4(R4), .in5(R5), .in6(R6), .in7(R7), .out(B), .sel(SelB));
  Register #(.width(15)) register_5 (.D(D), .en(W_4), .clk(CLK), .Q(R4));  // open: clr
  Register #(.width(15)) register_6 (.D(D), .en(W_5), .clk(CLK), .Q(R5));  // open: clr
  Register #(.width(15)) register_7 (.D(D), .en(W_6), .clk(CLK), .Q(R6));  // open: clr
  Register #(.width(15)) register_8 (.D(D), .en(W_7), .clk(CLK), .Q(R7));  // open: clr
endmodule

module ALU15 (
  input  [14:0] A,
  input  [14:0] B,
  input  [2:0] OP,
  input  CIN,
  input  OIN,
  output C,
  output O,
  output N,
  output Z,
  output [14:0] R
);
endmodule

module FLAGS8 (
  input  IRQ,
  input  [7:0] NF,
  input  [7:0] WM,
  input  CLK,
  output [7:0] F
);
endmodule

module IMM15 (
  input  [14:0] INST,
  output [14:0] SEXT
);

  wire and_1_out, and_2_out, and_3_out, and_4_out, and_6_out, and_7_out, Encode_0_a, Encode_0_b, Encode_0_c,
       Encode_1_a, Encode_2_a, not_6_out, not_7_out, NOT_OP_0, NOT_OP_1, NOT_OP_2, NOT_OP_3, NOT_OP_4;
  wire [2:0] or_5_out;

  and and_1 (and_1_out, INST[3], NOT_OP_4);
  and and_2 (and_2_out, INST[0], INST[1], NOT_OP_2, INST[3], INST[4]);
  and and_3 (and_3_out, INST[4], INST[3], INST[2], NOT_OP_1, NOT_OP_0);
  and and_4 (and_4_out, INST[4], INST[3], INST[2], NOT_OP_1, INST[0]);
  and and_5 (Encode_0_c, INST[4], INST[3], INST[2], INST[1], INST[0]);
  or or_1 (Encode_0_b, and_3_out, and_4_out);
  LED Bits_11 (.in(Encode_0_c));
  not not_1 (NOT_OP_0, INST[0]);
  not not_2 (NOT_OP_1, INST[1]);
  not not_3 (NOT_OP_2, INST[2]);
  not not_4 (NOT_OP_3, INST[3]);
  not not_5 (NOT_OP_4, INST[4]);
  or or_2 (Encode_0_a, and_1_out, and_2_out);
  LED Bits_4 (.in(Encode_0_a));
  LED Bits_7 (.in(Encode_0_b));
  Register #(.trigger("high"), .width(15)) register_1 (.D(SEXT), .en(1'b1), .clk(1'b1));  // open: Q, clr
  and and_6 (and_6_out, INST[2], INST[1], NOT_OP_0);
  and and_7 (and_7_out, INST[2], INST[1], INST[0]);
  or or_3 (or_5_out[2], Encode_0_c, Encode_2_a);
  not not_6 (not_6_out, and_6_out);
  not not_7 (not_7_out, and_7_out);
  or or_4 (or_5_out[1], Encode_0_b, Encode_1_a);
  and and_8 (Encode_1_a, INST[4], NOT_OP_3, not_6_out, not_7_out);
  and and_9 (Encode_2_a, INST[4], INST[3], INST[2], INST[1], NOT_OP_0);
  Multiplexer #(.select(3), .width(15)) multiplexer_1 (
    .in0({15{1'b0}}), .in1({{12{INST[14]}}, INST[13:11]}), .in2({{6{INST[14]}}, INST[13:5]}),
    .in3({{9{INST[14]}}, INST[13:8]}), .in4({{12{INST[14]}}, INST[7:5]}),
    .in5({{5{INST[14]}}, INST[13:8], 4'b0000}), .in6({15{1'b0}}), .in7({15{1'b0}}), .out(SEXT), .sel(or_5_out));
  LED Bits_10 (.in(Encode_1_a));
  or or_5 (or_5_out[0], Encode_0_c, Encode_0_b, Encode_0_a);
  LED Bits_4_SW (.in(Encode_2_a));

  // Other names for the same wires on the sheet: Bits_4_SW[14:0] = {{12{INST[14]}}, INST[7:5]};
  //   Bits_10[14:0] = {{6{INST[14]}}, INST[13:5]}; Bits_4[14:0] = {{12{INST[14]}}, INST[13:11]};
  //   Bits_7[14:0] = {{9{INST[14]}}, INST[13:8]}; Bits_11[14:4] = {{5{INST[14]}}, INST[13:8]};
  //   Encode_1_b = Encode_0_b; Encode_2_b = Encode_0_c; OP_0 = INST[0]; OP_1 = INST[1]; OP_2 = INST[2];
  //   OP_3 = INST[3]; OP_4 = INST[4]
endmodule

module DECODE15 (
  input  [4:0] OPCODE,
  output SWI,
  output STORE,
  output LOAD,
  output [1:0] ASEL,
  output [1:0] BSEL,
  output [2:0] ALUOP,
  output [2:0] REGDATASRC,
  output REGW,
  output [1:0] FLAGSRC,
  output [7:0] FLAGWM,
  output SRPW,
  output SRFW
);
endmodule
